// Logisim project CPU_8_BIT.circ as structural Verilog
module CPU_MEM_8 (
  input  [7:0] i,
  input  s,
  output [7:0] o
);

  D_Flip_Flop d_ff_1 (.D(i[0]), .clk(s), .Q(o[0]));  // open: Qn, preset, reset
  D_Flip_Flop d_ff_2 (.D(i[1]), .clk(s), .Q(o[1]));  // open: Qn, preset, reset
  D_Flip_Flop d_ff_3 (.D(i[2]), .clk(s), .Q(o[2]));  // open: Qn, preset, reset
  D_Flip_Flop d_ff_4 (.D(i[3]), .clk(s), .Q(o[3]));  // open: Qn, preset, reset
  D_Flip_Flop d_ff_5 (.D(i[4]), .clk(s), .Q(o[4]));  // open: Qn, preset, reset
  D_Flip_Flop d_ff_6 (.D(i[5]), .clk(s), .Q(o[5]));  // open: Qn, preset, reset
  D_Flip_Flop d_ff_7 (.D(i[6]), .clk(s), .Q(o[6]));  // open: Qn, preset, reset
  D_Flip_Flop d_ff_8 (.D(i[7]), .clk(s), .Q(o[7]));  // open: Qn, preset, reset
endmodule

module CPU_ENABLE (
  input  [7:0] i,
  input  e,
  output [7:0] o
);

  wire and_1_out, and_2_out, and_3_out, and_4_out, and_5_out, and_6_out, and_7_out, and_8_out;

  and and_1 (and_1_out, i[0], e);
  and and_2 (and_2_out, i[1], e);
  and and_3 (and_3_out, i[2], e);
  and and_4 (and_4_out, i[3], e);
  and and_5 (and_5_out, i[4], e);
  and and_6 (and_6_out, i[5], e);
  and and_7 (and_7_out, i[6], e);
  and and_8 (and_8_out, i[7], e);
  assign o[0] = e ? and_1_out : 1'bz;  // Controlled_Buffer controlled_buffer_1
  assign o[1] = e ? and_2_out : 1'bz;  // Controlled_Buffer controlled_buffer_2
  assign o[2] = e ? and_3_out : 1'bz;  // Controlled_Buffer controlled_buffer_3
  assign o[3] = e ? and_4_out : 1'bz;  // Controlled_Buffer controlled_buffer_4
  assign o[4] = e ? and_5_out : 1'bz;  // Controlled_Buffer controlled_buffer_5
  assign o[5] = e ? and_6_out : 1'bz;  // Controlled_Buffer controlled_buffer_6
  assign o[6] = e ? and_7_out : 1'bz;  // Controlled_Buffer controlled_buffer_7
  assign o[7] = e ? and_8_out : 1'bz;  // Controlled_Buffer controlled_buffer_8
endmodule

module CPU_REG_8 (
  input  [7:0] i,
  input  s,
  input  e,
  output [7:0] out_4,
  output [7:0] o
);

  wire [7:0] cpu_enable_1_o;

  CPU_MEM_8 cpu_mem_8_1 (.i(i), .s(s), .o(out_4));
  CPU_ENABLE cpu_enable_1 (.i(out_4), .e(e), .o(cpu_enable_1_o));
  assign o[0] = e ? cpu_enable_1_o[0] : 1'bz;  // Controlled_Buffer controlled_buffer_1
  // Pins of 1 and 8 bits meet at o
  // Pins of 1 and 8 bits meet at cpu_enable_1_o
endmodule

module CPU_DECODER_2_4 (
  input  in_1,
  input  in_2,
  output out_3,
  output out_4,
  output out_5,
  output out_6
);

  wire not_1_out, not_2_out;

  not not_1 (not_1_out, in_1);
  not not_2 (not_2_out, in_2);
  and and_1 (out_3, not_2_out, not_1_out);
  and and_2 (out_4, not_1_out, in_2);
  and and_3 (out_5, not_2_out, in_1);
  and and_4 (out_6, in_2, in_1);
endmodule

module CPU_REG_BYTE (
);

  wire and_1_out, cpu_reg_8_1_p2, undriven;

  buf and_1 (and_1_out, undriven);  // AND_Gate
  // CPU_REG_8 cpu_reg_8_1: pin names not known; wires that end beside it: and_1_out, cpu_reg_8_1_p2
  Controlled_Buffer controlled_buffer_1 (.in(cpu_reg_8_1_p2), .en(and_1_out));  // open: out
endmodule
