// Logisim project CPU_8_V2_S9.circ as structural Verilog: 35 circuits, main circuit main
module main (
  input  in_1,
  input  in_2,
  input  [7:0] in_3,
  input  in_4,
  input  in_5,
  input  in_6,
  input  in_7,
  input  in_8,
  input  in_9,
  input  in_10
);

  wire clock_1_out, s1, s2, s3, s4, s5, s6, s7, s8, s9;
  wire [7:0] ACC, BUS_0, controlled_buffer_1_out, IR, PC, PROG_D, R0, R1, R2, R3;

  Hex_Digit_Display hex_digit_display_1 (.value(R0[7:4]));  // open: dp
  Hex_Digit_Display hex_digit_display_2 (.value(R0[3:0]));  // open: dp
  Hex_Digit_Display hex_digit_display_3 (.value(PC[7:4]));  // open: dp
  Hex_Digit_Display hex_digit_display_4 (.value(PC[3:0]));  // open: dp
  Hex_Digit_Display hex_digit_display_5 (.value(R1[7:4]));  // open: dp
  Hex_Digit_Display hex_digit_display_6 (.value(R1[3:0]));  // open: dp
  Hex_Digit_Display hex_digit_display_7 (.value(IR[7:4]));  // open: dp
  Hex_Digit_Display hex_digit_display_8 (.value(IR[3:0]));  // open: dp
  Hex_Digit_Display hex_digit_display_9 (.value(R2[7:4]));  // open: dp
  Hex_Digit_Display hex_digit_display_10 (.value(ACC[7:4]));  // open: dp
  Hex_Digit_Display hex_digit_display_11 (.value(R2[3:0]));  // open: dp
  Hex_Digit_Display hex_digit_display_12 (.value(ACC[3:0]));  // open: dp
  Hex_Digit_Display hex_digit_display_13 (.value(R3[7:4]));  // open: dp
  Hex_Digit_Display hex_digit_display_14 (.value(BUS_0[7:4]));  // open: dp
  Hex_Digit_Display hex_digit_display_15 (.value(R3[3:0]));  // open: dp
  Hex_Digit_Display hex_digit_display_16 (.value(BUS_0[3:0]));  // open: dp
  LED led_1 (.in(s2));
  LED led_2 (.in(s1));
  assign controlled_buffer_1_out = in_1 ? BUS_0 : 8'bz;  // Controlled_Buffer controlled_buffer_1
  LED led_3 (.in(s3));
  LED led_4 (.in(s4));
  ROM rom_1 (.addr(controlled_buffer_1_out), .data(PROG_D));
  LED led_5 (.in(s5));
  LED led_6 (.in(s6));
  LED led_7 (.in(s7));
  LED led_8 (.in(s8));
  LED led_9 (.in(s9));
  Clock clock_1 (.out(clock_1_out));
  CPU cpu_1 (
    .R2_S(in_9), .IR_S(in_5), .R3_S(in_10), .LOAD_PROG(in_1), .rst(in_2), .PROG_D(PROG_D), .rst_RAM(in_6),
    .CLK(clock_1_out), .BUS_DATA_INSERT(in_3), .BUS_DATA_INSERT_E(in_7), .R0_S(in_4), .R1_S(in_8), .s3(s3),
    .s4(s4), .R2(R2), .s5(s5), .s6(s6), .s7(s7), .R3(R3), .s8(s8), .s9(s9), .ACC(ACC), .BUS_DATA(BUS_0),
    .R0(R0), .PC(PC), .s1(s1), .R1(R1), .IR(IR), .s2(s2));

  // Other names for the same wires on the sheet: BUS_E = in_7; BUS_I[7:0] = in_3; IR_S = in_5; LOAD = in_1;
  //   R0_S = in_4; R1_S = in_8; R2_S = in_9; R3_S = in_10; RST = in_2; RST_RAM = in_6

  // Notes on the sheet:
  //   R0
  //   PC 
  //   R1
  //   IR
  //   R2
  //   ACC
  //   SET REGISTERS
  //   R3
  //   BUS_0
  //   FETCH
  //   contents of rom_1 (hex, n*v repeats v):
  //   20 2 21 2 22 14 f2 56 c 84 40 6 70
  //   FETCH2
  //   LOAD PROGRAM
  //   EXECUTE
endmodule

module CPU_D_LATCH (
  input  s,
  input  e,
  output o
);

  wire nand_1_out, nand_2_out, nand_4_out;

  nand nand_1 (nand_1_out, s, e);
  nand nand_2 (nand_2_out, nand_1_out, e);
  nand nand_3 (o, nand_1_out, nand_4_out);
  nand nand_4 (nand_4_out, o, nand_2_out);
endmodule

module CPU_D_FLIP_FLOP (
  input  D,
  input  clk,
  output o
);

  wire nand_1_out, nand_2_out, nand_4_out, not_1_out;

  not not_1 (not_1_out, D);
  nand nand_1 (nand_1_out, D, clk);
  nand nand_2 (nand_2_out, not_1_out, clk);
  nand nand_3 (o, nand_1_out, nand_4_out);
  nand nand_4 (nand_4_out, o, nand_2_out);
endmodule

module CPU_MEM_8 (
  input  [7:0] i,
  input  s,
  input  rst,
  output [7:0] o
);

  D_Flip_Flop #(.trigger("high")) d_ff_1 (.D(i[0]), .clk(s), .Q(o[0]), .reset(rst));  // open: Qn, preset
  D_Flip_Flop #(.trigger("high")) d_ff_2 (.D(i[1]), .clk(s), .Q(o[1]), .reset(rst));  // open: Qn, preset
  D_Flip_Flop #(.trigger("high")) d_ff_3 (.D(i[2]), .clk(s), .Q(o[2]), .reset(rst));  // open: Qn, preset
  D_Flip_Flop #(.trigger("high")) d_ff_4 (.D(i[3]), .clk(s), .Q(o[3]), .reset(rst));  // open: Qn, preset
  D_Flip_Flop #(.trigger("high")) d_ff_5 (.D(i[4]), .clk(s), .Q(o[4]), .reset(rst));  // open: Qn, preset
  D_Flip_Flop #(.trigger("high")) d_ff_6 (.D(i[5]), .clk(s), .Q(o[5]), .reset(rst));  // open: Qn, preset
  D_Flip_Flop #(.trigger("high")) d_ff_7 (.D(i[6]), .clk(s), .Q(o[6]), .reset(rst));  // open: Qn, preset
  D_Flip_Flop #(.trigger("high")) d_ff_8 (.D(i[7]), .clk(s), .Q(o[7]), .reset(rst));  // open: Qn, preset
endmodule

module CPU_ENABLE (
  input  [7:0] i,
  input  e,
  output [7:0] o
);

  wire and_1_out, and_2_out, and_3_out, and_4_out, and_5_out, and_6_out, and_7_out, and_8_out;

  and and_1 (and_1_out, i[0], e);
  and and_2 (and_2_out, i[1], e);
  and and_3 (and_3_out, i[2], e);
  and and_4 (and_4_out, i[3], e);
  and and_5 (and_5_out, i[4], e);
  and and_6 (and_6_out, i[5], e);
  and and_7 (and_7_out, i[6], e);
  and and_8 (and_8_out, i[7], e);
  assign o[0] = e ? and_1_out : 1'bz;  // Controlled_Buffer controlled_buffer_1
  assign o[1] = e ? and_2_out : 1'bz;  // Controlled_Buffer controlled_buffer_2
  assign o[2] = e ? and_3_out : 1'bz;  // Controlled_Buffer controlled_buffer_3
  assign o[3] = e ? and_4_out : 1'bz;  // Controlled_Buffer controlled_buffer_4
  assign o[4] = e ? and_5_out : 1'bz;  // Controlled_Buffer controlled_buffer_5
  assign o[5] = e ? and_6_out : 1'bz;  // Controlled_Buffer controlled_buffer_6
  assign o[6] = e ? and_7_out : 1'bz;  // Controlled_Buffer controlled_buffer_7
  assign o[7] = e ? and_8_out : 1'bz;  // Controlled_Buffer controlled_buffer_8
endmodule

module CPU_REG_8 (
  input  rst,
  input  [7:0] i,
  input  e,
  input  s,
  output [7:0] r,
  output [7:0] o
);

  wire [7:0] cpu_enable_1_o;

  CPU_MEM_8 cpu_mem_8_1 (.i(i), .s(s), .rst(rst), .o(r));
  CPU_ENABLE cpu_enable_1 (.i(r), .e(e), .o(cpu_enable_1_o));
  assign o = e ? cpu_enable_1_o : 8'bz;  // Controlled_Buffer controlled_buffer_1
endmodule

module CPU_REG_BYTE (
  input  [7:0] i,
  input  v,
  input  h,
  input  rst,
  input  s,
  input  e,
  output [7:0] r,
  output [7:0] o
);

  wire and_1_out, and_2_out, and_3_out;
  wire [7:0] cpu_reg_8_1_o;

  and and_1 (and_1_out, v, h);
  and and_2 (and_2_out, and_1_out, s);
  and and_3 (and_3_out, and_1_out, e);
  CPU_REG_8 cpu_reg_8_1 (.i(i), .rst(rst), .s(and_2_out), .e(and_3_out), .o(cpu_reg_8_1_o), .r(r));
  assign o = and_3_out ? cpu_reg_8_1_o : 8'bz;  // Controlled_Buffer controlled_buffer_1
endmodule

module CPU_DECODER_2_4 (
  input  [1:0] i,
  output out_2,
  output out_3,
  output out_4,
  output out_5
);

  wire not_1_out, not_2_out;

  not not_1 (not_1_out, i[1]);
  not not_2 (not_2_out, i[0]);
  and and_1 (out_2, not_2_out, not_1_out);
  and and_2 (out_3, not_1_out, i[0]);
  and and_3 (out_4, not_2_out, i[1]);
  and and_4 (out_5, i[0], i[1]);
endmodule

module CPU_DECODER_3_8 (
  input  [2:0] in_1,
  output out_2,
  output out_3,
  output out_4,
  output out_5,
  output out_6,
  output out_7,
  output out_8,
  output out_9
);

  wire not_1_out, not_2_out, not_3_out;

  not not_1 (not_1_out, in_1[0]);
  not not_2 (not_2_out, in_1[1]);
  not not_3 (not_3_out, in_1[2]);
  and and_1 (out_2, not_1_out, not_2_out, not_3_out);
  and and_2 (out_3, not_2_out, not_3_out, in_1[0]);
  and and_3 (out_4, not_1_out, not_3_out, in_1[1]);
  and and_4 (out_5, not_3_out, in_1[0], in_1[1]);
  and and_5 (out_6, not_1_out, not_2_out, in_1[2]);
  and and_6 (out_7, not_2_out, in_1[0], in_1[2]);
  and and_7 (out_8, not_1_out, in_1[1], in_1[2]);
  and and_8 (out_9, in_1[0], in_1[1], in_1[2]);
endmodule

module CPU_DECODER_4_16 (
  input  [3:0] in_1,
  output out_2,
  output out_3,
  output out_4,
  output out_5,
  output out_6,
  output out_7,
  output out_8,
  output out_9,
  output out_10,
  output out_11,
  output out_12,
  output out_13,
  output out_14,
  output out_15,
  output out_16,
  output out_17
);

  wire not_1_out, not_2_out, not_3_out, not_4_out;

  not not_1 (not_1_out, in_1[0]);
  not not_2 (not_2_out, in_1[1]);
  not not_3 (not_3_out, in_1[2]);
  not not_4 (not_4_out, in_1[3]);
  and and_1 (out_2, not_4_out, not_3_out, not_2_out, not_1_out);
  and and_2 (out_3, not_4_out, not_3_out, not_2_out, in_1[0]);
  and and_3 (out_4, not_4_out, not_3_out, not_1_out, in_1[1]);
  and and_4 (out_5, not_4_out, not_3_out, in_1[0], in_1[1]);
  and and_5 (out_6, not_4_out, not_2_out, not_1_out, in_1[2]);
  and and_6 (out_7, not_4_out, not_2_out, in_1[0], in_1[2]);
  and and_7 (out_8, not_4_out, not_1_out, in_1[1], in_1[2]);
  and and_8 (out_9, not_4_out, in_1[0], in_1[1], in_1[2]);
  and and_9 (out_10, not_3_out, not_2_out, not_1_out, in_1[3]);
  and and_10 (out_11, not_3_out, not_2_out, in_1[0], in_1[3]);
  and and_11 (out_12, not_3_out, not_1_out, in_1[1], in_1[3]);
  and and_12 (out_13, not_3_out, in_1[0], in_1[1], in_1[3]);
  and and_13 (out_14, not_2_out, not_1_out, in_1[2], in_1[3]);
  and and_14 (out_15, not_2_out, in_1[0], in_1[2], in_1[3]);
  and and_15 (out_16, not_1_out, in_1[1], in_1[2], in_1[3]);
  and and_16 (out_17, in_1[0], in_1[1], in_1[2], in_1[3]);
endmodule

module RAM_256 (
  input  [7:0] address,
  input  sa,
  input  [7:0] i,
  input  rst,
  input  s,
  input  e,
  output [7:0] o,
  output [7:0] out_8,
  output [7:0] out_9,
  output [7:0] out_10,
  output [7:0] out_11,
  output [7:0] out_12,
  output [7:0] out_13,
  output [7:0] out_14,
  output [7:0] out_15,
  output [7:0] out_16,
  output [7:0] out_17,
  output [7:0] out_18,
  output [7:0] out_19,
  output [7:0] out_20,
  output [7:0] out_21,
  output [7:0] out_22,
  output [7:0] out_23,
  output [7:0] out_24,
  output [7:0] out_25,
  output [7:0] out_26,
  output [7:0] out_27,
  output [7:0] out_28,
  output [7:0] out_29,
  output [7:0] out_30,
  output [7:0] out_31,
  output [7:0] out_32,
  output [7:0] out_33,
  output [7:0] out_34,
  output [7:0] out_35,
  output [7:0] out_36,
  output [7:0] out_37,
  output [7:0] out_38,
  output [7:0] out_39
);

  wire cpu_decoder_4_16_1_out_2, cpu_decoder_4_16_1_out_3, cpu_decoder_4_16_1_out_4,
       cpu_decoder_4_16_2_out_2, cpu_decoder_4_16_2_out_3, cpu_decoder_4_16_2_out_4,
       cpu_decoder_4_16_2_out_5, cpu_decoder_4_16_2_out_6, cpu_decoder_4_16_2_out_7,
       cpu_decoder_4_16_2_out_8, cpu_decoder_4_16_2_out_9, cpu_decoder_4_16_2_out_10,
       cpu_decoder_4_16_2_out_11, cpu_decoder_4_16_2_out_12, cpu_decoder_4_16_2_out_13,
       cpu_decoder_4_16_2_out_14, cpu_decoder_4_16_2_out_15, cpu_decoder_4_16_2_out_16,
       cpu_decoder_4_16_2_out_17;
  wire [7:0] cpu_mem_8_1_o, cpu_reg_byte_1_o;

  CPU_MEM_8 cpu_mem_8_1 (.i(address), .s(sa), .o(cpu_mem_8_1_o));  // open: rst
  CPU_DECODER_4_16 cpu_decoder_4_16_1 (
    .in_1(cpu_mem_8_1_o[7:4]), .out_2(cpu_decoder_4_16_1_out_2), .out_3(cpu_decoder_4_16_1_out_3),
    .out_4(cpu_decoder_4_16_1_out_4));  // open: out_8, out_9, out_10, out_11, out_12, out_13, out_14, out_15, out_16, out_17, out_5, out_6, out_7
  assign o = e ? cpu_reg_byte_1_o : 8'bz;  // Controlled_Buffer controlled_buffer_1
  CPU_REG_BYTE cpu_reg_byte_1 (
    .v(cpu_decoder_4_16_2_out_17), .h(cpu_decoder_4_16_1_out_2), .s(s), .e(e), .i(i), .rst(rst), .r(out_8),
    .o(cpu_reg_byte_1_o));
  CPU_REG_BYTE cpu_reg_byte_2 (
    .v(cpu_decoder_4_16_2_out_17), .h(cpu_decoder_4_16_1_out_3), .s(s), .e(e), .i(i), .rst(rst), .r(out_24),
    .o(cpu_reg_byte_1_o));
  CPU_REG_BYTE cpu_reg_byte_3 (
    .v(cpu_decoder_4_16_2_out_16), .h(cpu_decoder_4_16_1_out_2), .s(s), .e(e), .i(i), .rst(rst), .r(out_9),
    .o(cpu_reg_byte_1_o));
  CPU_REG_BYTE cpu_reg_byte_4 (
    .v(cpu_decoder_4_16_2_out_16), .h(cpu_decoder_4_16_1_out_3), .s(s), .e(e), .i(i), .rst(rst), .r(out_25),
    .o(cpu_reg_byte_1_o));
  CPU_REG_BYTE cpu_reg_byte_5 (
    .v(cpu_decoder_4_16_2_out_15), .h(cpu_decoder_4_16_1_out_2), .s(s), .e(e), .i(i), .rst(rst), .r(out_10),
    .o(cpu_reg_byte_1_o));
  CPU_REG_BYTE cpu_reg_byte_6 (
    .v(cpu_decoder_4_16_2_out_15), .h(cpu_decoder_4_16_1_out_3), .s(s), .e(e), .i(i), .rst(rst), .r(out_26),
    .o(cpu_reg_byte_1_o));
  CPU_REG_BYTE cpu_reg_byte_7 (
    .v(cpu_decoder_4_16_2_out_14), .h(cpu_decoder_4_16_1_out_2), .s(s), .e(e), .i(i), .rst(rst), .r(out_11),
    .o(cpu_reg_byte_1_o));
  CPU_REG_BYTE cpu_reg_byte_8 (
    .v(cpu_decoder_4_16_2_out_14), .h(cpu_decoder_4_16_1_out_3), .s(s), .e(e), .i(i), .rst(rst), .r(out_27),
    .o(cpu_reg_byte_1_o));
  CPU_REG_BYTE cpu_reg_byte_9 (
    .v(cpu_decoder_4_16_2_out_13), .h(cpu_decoder_4_16_1_out_2), .s(s), .e(e), .i(i), .rst(rst), .r(out_12),
    .o(cpu_reg_byte_1_o));
  CPU_REG_BYTE cpu_reg_byte_10 (
    .v(cpu_decoder_4_16_2_out_13), .h(cpu_decoder_4_16_1_out_3), .s(s), .e(e), .i(i), .rst(rst), .r(out_28),
    .o(cpu_reg_byte_1_o));
  CPU_REG_BYTE cpu_reg_byte_11 (
    .v(cpu_decoder_4_16_2_out_12), .h(cpu_decoder_4_16_1_out_2), .s(s), .e(e), .i(i), .rst(rst), .r(out_13),
    .o(cpu_reg_byte_1_o));
  CPU_REG_BYTE cpu_reg_byte_12 (
    .v(cpu_decoder_4_16_2_out_12), .h(cpu_decoder_4_16_1_out_3), .s(s), .e(e), .i(i), .rst(rst), .r(out_29),
    .o(cpu_reg_byte_1_o));
  CPU_REG_BYTE cpu_reg_byte_13 (
    .v(cpu_decoder_4_16_2_out_11), .h(cpu_decoder_4_16_1_out_2), .s(s), .e(e), .i(i), .rst(rst), .r(out_14),
    .o(cpu_reg_byte_1_o));
  CPU_REG_BYTE cpu_reg_byte_14 (
    .v(cpu_decoder_4_16_2_out_11), .h(cpu_decoder_4_16_1_out_3), .s(s), .e(rst), .i(i), .rst(rst),
    .r(out_30), .o(cpu_reg_byte_1_o));
  CPU_REG_BYTE cpu_reg_byte_15 (
    .v(cpu_decoder_4_16_2_out_10), .h(cpu_decoder_4_16_1_out_2), .s(s), .e(e), .i(i), .rst(rst), .r(out_15),
    .o(cpu_reg_byte_1_o));
  CPU_REG_BYTE cpu_reg_byte_16 (
    .v(cpu_decoder_4_16_2_out_10), .h(cpu_decoder_4_16_1_out_3), .s(s), .e(e), .i(i), .rst(rst), .r(out_31),
    .o(cpu_reg_byte_1_o));
  CPU_REG_BYTE cpu_reg_byte_17 (
    .v(cpu_decoder_4_16_2_out_9), .h(cpu_decoder_4_16_1_out_2), .s(s), .e(e), .i(i), .rst(rst), .r(out_16),
    .o(cpu_reg_byte_1_o));
  CPU_REG_BYTE cpu_reg_byte_18 (
    .v(cpu_decoder_4_16_2_out_9), .h(cpu_decoder_4_16_1_out_3), .s(s), .e(e), .i(i), .rst(rst), .r(out_32),
    .o(cpu_reg_byte_1_o));
  CPU_REG_BYTE cpu_reg_byte_19 (
    .v(cpu_decoder_4_16_2_out_8), .h(cpu_decoder_4_16_1_out_2), .s(s), .e(e), .i(i), .rst(rst), .r(out_17),
    .o(cpu_reg_byte_1_o));
  CPU_REG_BYTE cpu_reg_byte_20 (
    .v(cpu_decoder_4_16_2_out_8), .h(cpu_decoder_4_16_1_out_3), .s(s), .e(e), .i(i), .rst(rst), .r(out_33),
    .o(cpu_reg_byte_1_o));
  CPU_REG_BYTE cpu_reg_byte_21 (
    .v(cpu_decoder_4_16_2_out_7), .h(cpu_decoder_4_16_1_out_2), .s(s), .e(e), .i(i), .rst(rst), .r(out_18),
    .o(cpu_reg_byte_1_o));
  CPU_REG_BYTE cpu_reg_byte_22 (
    .v(cpu_decoder_4_16_2_out_7), .h(cpu_decoder_4_16_1_out_3), .s(s), .e(e), .i(i), .rst(rst), .r(out_34),
    .o(cpu_reg_byte_1_o));
  CPU_REG_BYTE cpu_reg_byte_23 (
    .v(cpu_decoder_4_16_2_out_6), .h(cpu_decoder_4_16_1_out_2), .s(s), .e(e), .i(i), .rst(rst), .r(out_19),
    .o(cpu_reg_byte_1_o));
  CPU_REG_BYTE cpu_reg_byte_24 (
    .v(cpu_decoder_4_16_2_out_6), .h(cpu_decoder_4_16_1_out_3), .s(s), .e(e), .i(i), .rst(rst), .r(out_35),
    .o(cpu_reg_byte_1_o));
  CPU_REG_BYTE cpu_reg_byte_25 (
    .v(cpu_decoder_4_16_2_out_5), .h(cpu_decoder_4_16_1_out_2), .s(s), .e(e), .i(i), .rst(rst), .r(out_20),
    .o(cpu_reg_byte_1_o));
  CPU_REG_BYTE cpu_reg_byte_26 (
    .v(cpu_decoder_4_16_2_out_5), .h(cpu_decoder_4_16_1_out_3), .s(s), .e(e), .i(i), .rst(rst), .r(out_36),
    .o(cpu_reg_byte_1_o));
  CPU_REG_BYTE cpu_reg_byte_27 (
    .v(cpu_decoder_4_16_2_out_4), .h(cpu_decoder_4_16_1_out_2), .s(s), .e(e), .i(i), .rst(rst), .r(out_21),
    .o(cpu_reg_byte_1_o));
  CPU_REG_BYTE cpu_reg_byte_28 (
    .v(cpu_decoder_4_16_2_out_4), .h(cpu_decoder_4_16_1_out_3), .s(s), .e(e), .i(i), .rst(rst), .r(out_37),
    .o(cpu_reg_byte_1_o));
  CPU_REG_BYTE cpu_reg_byte_29 (
    .v(cpu_decoder_4_16_2_out_3), .h(cpu_decoder_4_16_1_out_2), .s(s), .e(e), .i(i), .rst(rst), .r(out_22),
    .o(cpu_reg_byte_1_o));
  CPU_REG_BYTE cpu_reg_byte_30 (
    .v(cpu_decoder_4_16_2_out_3), .h(cpu_decoder_4_16_1_out_3), .s(s), .e(e), .i(i), .rst(rst), .r(out_38),
    .o(cpu_reg_byte_1_o));
  CPU_REG_BYTE cpu_reg_byte_31 (
    .v(cpu_decoder_4_16_2_out_2), .h(cpu_decoder_4_16_1_out_2), .s(s), .e(e), .i(i), .rst(rst), .r(out_23),
    .o(cpu_reg_byte_1_o));
  CPU_REG_BYTE cpu_reg_byte_32 (
    .v(cpu_decoder_4_16_2_out_2), .h(cpu_decoder_4_16_1_out_3), .s(s), .e(e), .i(i), .rst(rst), .r(out_39),
    .o(cpu_reg_byte_1_o));
  CPU_DECODER_4_16 cpu_decoder_4_16_2 (
    .in_1(cpu_mem_8_1_o[3:0]), .out_8(cpu_decoder_4_16_2_out_8), .out_9(cpu_decoder_4_16_2_out_9),
    .out_10(cpu_decoder_4_16_2_out_10), .out_11(cpu_decoder_4_16_2_out_11),
    .out_12(cpu_decoder_4_16_2_out_12), .out_13(cpu_decoder_4_16_2_out_13),
    .out_14(cpu_decoder_4_16_2_out_14), .out_15(cpu_decoder_4_16_2_out_15),
    .out_16(cpu_decoder_4_16_2_out_16), .out_17(cpu_decoder_4_16_2_out_17), .out_2(cpu_decoder_4_16_2_out_2),
    .out_3(cpu_decoder_4_16_2_out_3), .out_4(cpu_decoder_4_16_2_out_4), .out_5(cpu_decoder_4_16_2_out_5),
    .out_6(cpu_decoder_4_16_2_out_6), .out_7(cpu_decoder_4_16_2_out_7));
endmodule

module CPU_SHR (
  input  [7:0] a,
  input  si,
  output so,
  output [7:0] o
);

  wire [7:1] cpu_reg_8_1_o;

  CPU_REG_8 cpu_reg_8_1 (.i(a), .s(1'b1), .e(1'b1), .o({cpu_reg_8_1_o, so}));  // open: rst, r
  CPU_REG_8 cpu_reg_8_2 (.i({si, cpu_reg_8_1_o}), .s(1'b1), .e(1'b1), .o(o));  // open: rst, r
endmodule

module CPU_SHL (
  input  si,
  input  [7:0] a,
  output [7:0] o,
  output so
);

  wire [6:0] cpu_reg_8_1_o;

  CPU_REG_8 cpu_reg_8_1 (.i(a), .s(1'b1), .e(1'b1), .o({so, cpu_reg_8_1_o}));  // open: rst, r
  CPU_REG_8 cpu_reg_8_2 (.i({cpu_reg_8_1_o, si}), .s(1'b1), .e(1'b1), .o(o));  // open: rst, r
endmodule

module CPU_NOT (
  input  [7:0] a,
  output [7:0] o
);

  not not_1 (o[0], a[0]);
  not not_2 (o[1], a[1]);
  not not_3 (o[2], a[2]);
  not not_4 (o[3], a[3]);
  not not_5 (o[4], a[4]);
  not not_6 (o[5], a[5]);
  not not_7 (o[6], a[6]);
  not not_8 (o[7], a[7]);
endmodule

module CPU_OR (
  input  [7:0] a,
  input  [7:0] b,
  output [7:0] o
);

  or or_1 (o[0], a[0], b[0]);
  or or_2 (o[1], a[1], b[1]);
  or or_3 (o[2], a[2], b[2]);
  or or_4 (o[3], a[3], b[3]);
  or or_5 (o[4], a[4], b[4]);
  or or_6 (o[5], a[5], b[5]);
  or or_7 (o[6], a[6], b[6]);
  or or_8 (o[7], a[7], b[7]);
endmodule

module CPU_AND (
  input  [7:0] a,
  input  [7:0] b,
  output [7:0] o
);

  and and_1 (o[0], a[0], b[0]);
  and and_2 (o[1], a[1], b[1]);
  and and_3 (o[2], a[2], b[2]);
  and and_4 (o[3], a[3], b[3]);
  and and_5 (o[4], a[4], b[4]);
  and and_6 (o[5], a[5], b[5]);
  and and_7 (o[6], a[6], b[6]);
  and and_8 (o[7], a[7], b[7]);
endmodule

module CPU_XOR (
  input  [7:0] a,
  input  [7:0] b,
  output [7:0] o
);

  xor xor_1 (o[0], a[0], b[0]);
  xor xor_2 (o[1], a[1], b[1]);
  xor xor_3 (o[2], a[2], b[2]);
  xor xor_4 (o[3], a[3], b[3]);
  xor xor_5 (o[4], a[4], b[4]);
  xor xor_6 (o[5], a[5], b[5]);
  xor xor_7 (o[6], a[6], b[6]);
  xor xor_8 (o[7], a[7], b[7]);
endmodule

module CPU_ADDER (
  input  a,
  input  b,
  input  c_in,
  output s,
  output c_out
);

  wire and_1_out, and_2_out, xor_1_out;

  xor xor_1 (xor_1_out, a, b);
  and and_1 (and_1_out, c_in, xor_1_out);
  and and_2 (and_2_out, a, b);
  xor xor_2 (s, xor_1_out, c_in);
  or or_1 (c_out, and_1_out, and_2_out);
endmodule

module CPU_ADDER_8 (
  input  c_in,
  input  [7:0] a,
  input  [7:0] b,
  output [7:0] s,
  output c_out
);

  wire cpu_adder_1_c_out, cpu_adder_2_c_out, cpu_adder_3_c_out, cpu_adder_4_c_out, cpu_adder_5_c_out,
       cpu_adder_6_c_out, cpu_adder_7_c_out;

  CPU_ADDER cpu_adder_1 (.a(a[0]), .b(b[0]), .c_in(c_in), .s(s[0]), .c_out(cpu_adder_1_c_out));
  CPU_ADDER cpu_adder_2 (.a(a[1]), .b(b[1]), .c_in(cpu_adder_1_c_out), .s(s[1]), .c_out(cpu_adder_2_c_out));
  CPU_ADDER cpu_adder_3 (.a(a[2]), .b(b[2]), .c_in(cpu_adder_2_c_out), .s(s[2]), .c_out(cpu_adder_3_c_out));
  CPU_ADDER cpu_adder_4 (.a(a[3]), .b(b[3]), .c_in(cpu_adder_3_c_out), .s(s[3]), .c_out(cpu_adder_4_c_out));
  CPU_ADDER cpu_adder_5 (.a(a[4]), .b(b[4]), .c_in(cpu_adder_4_c_out), .s(s[4]), .c_out(cpu_adder_5_c_out));
  CPU_ADDER cpu_adder_6 (.a(a[5]), .b(b[5]), .c_in(cpu_adder_5_c_out), .s(s[5]), .c_out(cpu_adder_6_c_out));
  CPU_ADDER cpu_adder_7 (.a(a[6]), .b(b[6]), .c_in(cpu_adder_6_c_out), .s(s[6]), .c_out(cpu_adder_7_c_out));
  CPU_ADDER cpu_adder_8 (.a(a[7]), .b(b[7]), .c_in(cpu_adder_7_c_out), .s(s[7]), .c_out(c_out));
endmodule

module CPU_XOR_LE_1 (
  input  a_greater,
  input  above_equal,
  input  a,
  input  b,
  output b_great,
  output a_great,
  output equal
);

  wire and_2_out, not_1_out;

  xor xor_1 (b_great, a, b);
  not not_1 (not_1_out, b_great);
  and and_1 (equal, not_1_out, above_equal);
  and and_2 (and_2_out, a, above_equal, b_great);
  or or_1 (a_great, and_2_out, a_greater);
endmodule

module CPU_XOR_LE_8 (
  input  [7:0] a,
  input  [7:0] b,
  output [7:0] o,
  output a_great,
  output equal
);

  wire cpu_xor_le_1_1_a_great, cpu_xor_le_1_1_equal, cpu_xor_le_1_2_a_great, cpu_xor_le_1_2_equal,
       cpu_xor_le_1_3_a_great, cpu_xor_le_1_3_equal, cpu_xor_le_1_4_a_great, cpu_xor_le_1_4_equal,
       cpu_xor_le_1_5_a_great, cpu_xor_le_1_5_equal, cpu_xor_le_1_6_a_great, cpu_xor_le_1_6_equal,
       cpu_xor_le_1_7_a_great, cpu_xor_le_1_7_equal;

  CPU_XOR_LE_1 cpu_xor_le_1_1 (
    .a(a[7]), .b(b[7]), .above_equal(1'b1), .a_greater(1'b0), .equal(cpu_xor_le_1_1_equal),
    .a_great(cpu_xor_le_1_1_a_great), .b_great(o[7]));
  CPU_XOR_LE_1 cpu_xor_le_1_2 (
    .a(a[6]), .b(b[6]), .above_equal(cpu_xor_le_1_1_equal), .a_greater(cpu_xor_le_1_1_a_great),
    .equal(cpu_xor_le_1_2_equal), .a_great(cpu_xor_le_1_2_a_great), .b_great(o[6]));
  CPU_XOR_LE_1 cpu_xor_le_1_3 (
    .a(a[5]), .b(b[5]), .above_equal(cpu_xor_le_1_2_equal), .a_greater(cpu_xor_le_1_2_a_great),
    .equal(cpu_xor_le_1_3_equal), .a_great(cpu_xor_le_1_3_a_great), .b_great(o[5]));
  CPU_XOR_LE_1 cpu_xor_le_1_4 (
    .a(a[4]), .b(b[4]), .above_equal(cpu_xor_le_1_3_equal), .a_greater(cpu_xor_le_1_3_a_great),
    .equal(cpu_xor_le_1_4_equal), .a_great(cpu_xor_le_1_4_a_great), .b_great(o[4]));
  CPU_XOR_LE_1 cpu_xor_le_1_5 (
    .a(a[3]), .b(b[3]), .above_equal(cpu_xor_le_1_4_equal), .a_greater(cpu_xor_le_1_4_a_great),
    .equal(cpu_xor_le_1_5_equal), .a_great(cpu_xor_le_1_5_a_great), .b_great(o[3]));
  CPU_XOR_LE_1 cpu_xor_le_1_6 (
    .a(a[2]), .b(b[2]), .above_equal(cpu_xor_le_1_5_equal), .a_greater(cpu_xor_le_1_5_a_great),
    .equal(cpu_xor_le_1_6_equal), .a_great(cpu_xor_le_1_6_a_great), .b_great(o[2]));
  CPU_XOR_LE_1 cpu_xor_le_1_7 (
    .a(a[1]), .b(b[1]), .above_equal(cpu_xor_le_1_6_equal), .a_greater(cpu_xor_le_1_6_a_great),
    .equal(cpu_xor_le_1_7_equal), .a_great(cpu_xor_le_1_7_a_great), .b_great(o[1]));
  CPU_XOR_LE_1 cpu_xor_le_1_8 (
    .a(a[0]), .b(b[0]), .above_equal(cpu_xor_le_1_7_equal), .a_greater(cpu_xor_le_1_7_a_great),
    .equal(equal), .a_great(a_great), .b_great(o[0]));
endmodule

module CPU_Z (
  input  [7:0] i,
  output o
);

  wire or_1_out;

  or or_1 (or_1_out, i[0], i[1], i[2], i[3], i[4], i[5], i[6], i[7]);
  not not_1 (o, or_1_out);
endmodule

module CPU_ALU (
  input  ALU_0,
  input  ALU_1,
  input  ALU_2,
  input  [7:0] a,
  input  [7:0] b,
  input  c_in,
  output equal,
  output a_greater,
  output zero,
  output [7:0] o,
  output c_out
);

  wire and_1_out, and_2_out, and_3_out, cpu_adder_8_1_c_out, cpu_decoder_3_8_1_out_2,
       cpu_decoder_3_8_1_out_3, cpu_decoder_3_8_1_out_4, cpu_decoder_3_8_1_out_5, cpu_decoder_3_8_1_out_6,
       cpu_decoder_3_8_1_out_7, cpu_decoder_3_8_1_out_8, cpu_shl_1_so, cpu_shr_1_so;
  wire [7:0] cpu_adder_8_1_s, cpu_and_1_o, cpu_not_1_o, cpu_or_1_o, cpu_shl_1_o, cpu_shr_1_o,
       cpu_xor_le_8_1_o;

  CPU_XOR_LE_8 cpu_xor_le_8_1 (.a(a), .b(b), .a_great(a_greater), .equal(equal), .o(cpu_xor_le_8_1_o));
  CPU_AND cpu_and_1 (.a(a), .b(b), .o(cpu_and_1_o));
  CPU_OR cpu_or_1 (.a(a), .b(b), .o(cpu_or_1_o));
  CPU_NOT cpu_not_1 (.a(a), .o(cpu_not_1_o));
  CPU_SHR cpu_shr_1 (.a(a), .si(c_in), .so(cpu_shr_1_so), .o(cpu_shr_1_o));
  CPU_SHL cpu_shl_1 (.a(a), .si(c_in), .so(cpu_shl_1_so), .o(cpu_shl_1_o));
  CPU_ADDER_8 cpu_adder_8_1 (.a(a), .b(b), .c_in(c_in), .c_out(cpu_adder_8_1_c_out), .s(cpu_adder_8_1_s));
  CPU_DECODER_3_8 cpu_decoder_3_8_1 (
    .in_1({ALU_2, ALU_1, ALU_0}), .out_2(cpu_decoder_3_8_1_out_2), .out_3(cpu_decoder_3_8_1_out_3),
    .out_4(cpu_decoder_3_8_1_out_4), .out_5(cpu_decoder_3_8_1_out_5), .out_6(cpu_decoder_3_8_1_out_6),
    .out_7(cpu_decoder_3_8_1_out_7), .out_8(cpu_decoder_3_8_1_out_8));  // open: out_9
  CPU_ENABLE cpu_enable_1 (.i(cpu_xor_le_8_1_o), .e(cpu_decoder_3_8_1_out_8), .o(o));
  CPU_ENABLE cpu_enable_2 (.i(cpu_and_1_o), .e(cpu_decoder_3_8_1_out_7), .o(o));
  CPU_ENABLE cpu_enable_3 (.i(cpu_or_1_o), .e(cpu_decoder_3_8_1_out_6), .o(o));
  CPU_ENABLE cpu_enable_4 (.i(cpu_not_1_o), .e(cpu_decoder_3_8_1_out_5), .o(o));
  CPU_ENABLE cpu_enable_5 (.i(cpu_shr_1_o), .e(cpu_decoder_3_8_1_out_4), .o(o));
  CPU_ENABLE cpu_enable_6 (.i(cpu_shl_1_o), .e(cpu_decoder_3_8_1_out_3), .o(o));
  CPU_ENABLE cpu_enable_7 (.i(cpu_adder_8_1_s), .e(cpu_decoder_3_8_1_out_2), .o(o));
  and and_1 (and_1_out, cpu_shr_1_so, cpu_decoder_3_8_1_out_4);
  assign c_out = cpu_decoder_3_8_1_out_4 ? and_1_out : 1'bz;  // Controlled_Buffer controlled_buffer_1
  and and_2 (and_2_out, cpu_shl_1_so, cpu_decoder_3_8_1_out_3);
  assign c_out = cpu_decoder_3_8_1_out_3 ? and_2_out : 1'bz;  // Controlled_Buffer controlled_buffer_2
  and and_3 (and_3_out, cpu_adder_8_1_c_out, cpu_decoder_3_8_1_out_2);
  assign c_out = cpu_decoder_3_8_1_out_2 ? and_3_out : 1'bz;  // Controlled_Buffer controlled_buffer_3
  CPU_Z cpu_z_1 (.i(o), .o(zero));
endmodule

module CPU_CLK (
  input  clkin,
  output clk,
  output clks,
  output clke
);

  wire j_k_ff_1_qn, nand_1_out;

  J_K_Flip_Flop j_k_ff_1 (.J(1'b1), .K(1'b1), .clk(clkin), .Q(clk), .Qn(j_k_ff_1_qn));  // open: preset, reset
  nand nand_1 (nand_1_out, clkin, clk);
  not not_1 (clks, nand_1_out);
  nand nand_2 (clke, j_k_ff_1_qn, clkin);
endmodule

module CPU_ACCUMULATOR (
  input  [7:0] i,
  input  s,
  input  e,
  output [7:0] r,
  output [7:0] o
);

  CPU_REG_8 cpu_reg_8_1 (.i(i), .s(s), .e(e), .o(o), .r(r));  // open: rst
endmodule

module CPU_TMP (
  input  [7:0] i,
  input  s,
  output [7:0] o
);

  CPU_MEM_8 cpu_mem_8_1 (.i(i), .s(s), .o(o));  // open: rst
endmodule

module CPU_BUS1 (
  input  [7:0] i,
  input  bus1,
  output [7:0] o
);

  wire not_1_out;

  and and_1 (o[7], i[7], not_1_out);
  and and_2 (o[6], i[6], not_1_out);
  and and_3 (o[5], i[5], not_1_out);
  and and_4 (o[4], i[4], not_1_out);
  and and_5 (o[3], i[3], not_1_out);
  and and_6 (o[2], i[2], not_1_out);
  and and_7 (o[1], i[1], not_1_out);
  or or_1 (o[0], i[0], bus1);
  not not_1 (not_1_out, bus1);
endmodule

module CPU_CONTROL_SECTION (
  input  clks,
  input  clk,
  input  clke,
  input  rst,
  input  LOAD_PROG,
  input  FLAG_C,
  input  [7:0] IR,
  input  FLAG_A,
  input  FLAG_E,
  input  FLAG_Z,
  output IAR_S,
  output s1,
  output s2,
  output s3,
  output s4,
  output s5,
  output s6,
  output s7,
  output s8,
  output s9,
  output BUS1_S,
  output IR_S,
  output RAM_E,
  output MAR_S,
  output ACC_E,
  output ACC_S,
  output IAR_E,
  output RAM_S,
  output TMP_S,
  output FLAG_S,
  output HALT,
  output R0_S,
  output R1_S,
  output R0_E,
  output R2_S,
  output R3_S,
  output R1_E,
  output R2_E,
  output R3_E,
  output ALU_0,
  output ALU_1,
  output ALU_2
);

  wire ACC_E_t, ACC_S_t, and_1_out, and_2_out, and_3_out, and_4_out, and_5_out, and_6_out, and_7_out,
       and_8_out, and_11_out, and_13_out, and_15_out, and_26_out, and_27_out, and_33_out, and_34_out,
       and_35_out, and_36_out, and_37_out, and_38_out, and_39_out, and_40_out, and_41_out, and_42_out,
       and_43_out, and_44_out, and_45_out, and_46_out, and_47_out, and_48_out, and_49_out, and_50_out,
       and_51_out, and_52_out, and_53_out, and_54_out, and_55_out, and_56_out, and_57_out, and_58_out,
       and_59_out, and_60_out, and_62_out, and_63_out, BUS1_S_t, CLF, controlled_buffer_30_out,
       cpu_decoder_3_8_1_out_2, cpu_decoder_3_8_1_out_3, cpu_decoder_3_8_1_out_4, cpu_decoder_3_8_1_out_5,
       cpu_decoder_3_8_1_out_6, cpu_decoder_3_8_1_out_7, cpu_decoder_3_8_1_out_8, cpu_decoder_3_8_1_out_9,
       cpu_stepper_1_s1, decoder_1_out1, decoder_1_out2, decoder_1_out3, decoder_1_out4, decoder_1_out5,
       decoder_1_out6, decoder_1_out7, decoder_1_out8, decoder_1_out9, decoder_1_out10, decoder_1_out11,
       decoder_1_out12, decoder_1_out13, decoder_1_out14, decoder_1_out15, DI, ESC, FLAG_S_t, HALT_t,
       IAR_E_t, IAR_S_t, IR_S_t, JMPR_A, JMPR_IF, JMPR_RB, LOAD, MAR_S_t, not_1_out, not_2_out, not_3_out,
       not_4_out, not_5_out, not_6_out, not_7_out, not_8_out, not_9_out, not_10_out, not_11_out, not_12_out,
       not_13_out, or_5_out, or_6_out, or_7_out, or_15_out, or_16_out, RAM_E_t, RAM_S_t, REG_A_E, REG_B_E,
       REG_B_S, STORE, TMP_S_t;
  wire [3:0] cpu_decoder_2_4_1_out_2, cpu_decoder_2_4_2_out_2, cpu_decoder_2_4_3_out_2;

  or or_1 (R0_E, and_1_out, and_5_out);
  or or_2 (R1_E, and_2_out, and_6_out);
  or or_3 (R2_E, and_3_out, and_7_out);
  or or_4 (R3_E, and_4_out, and_8_out);
  and and_1 (and_1_out, REG_B_E, cpu_decoder_2_4_1_out_2[0], clke);
  and and_2 (and_2_out, REG_B_E, cpu_decoder_2_4_1_out_2[1], clke);
  and and_3 (and_3_out, REG_B_E, cpu_decoder_2_4_1_out_2[2], clke);
  and and_4 (and_4_out, REG_B_E, cpu_decoder_2_4_1_out_2[3], clke);
  and and_5 (and_5_out, REG_A_E, cpu_decoder_2_4_2_out_2[0], clke);
  and and_6 (and_6_out, REG_A_E, cpu_decoder_2_4_2_out_2[1], clke);
  and and_7 (and_7_out, REG_A_E, cpu_decoder_2_4_2_out_2[2], clke);
  and and_8 (and_8_out, REG_A_E, cpu_decoder_2_4_2_out_2[3], clke);
  not not_1 (not_1_out, rst);
  and and_9 (BUS1_S, not_1_out, BUS1_S_t);
  and and_10 (RAM_E, not_1_out, and_11_out);
  and and_11 (and_11_out, clke, RAM_E_t);
  and and_12 (ACC_E, not_1_out, and_13_out);
  and and_13 (and_13_out, clke, ACC_E_t);
  and and_14 (IAR_E, not_1_out, and_15_out);
  and and_15 (and_15_out, clke, IAR_E_t);
  and and_16 (ALU_0, IR[7], s8, IR[4]);
  and and_17 (ALU_1, IR[7], s8, IR[5]);
  and and_18 (ALU_2, IR[7], s8, IR[6]);
  Pull_Resistor pull_resistor_1 (.node(BUS1_S_t));
  Pull_Resistor pull_resistor_2 (.node(RAM_E_t));
  Pull_Resistor pull_resistor_3 (.node(ACC_E_t));
  Pull_Resistor pull_resistor_4 (.node(IAR_E_t));
  Pull_Resistor pull_resistor_5 (.node(REG_B_E));
  Pull_Resistor pull_resistor_6 (.node(REG_A_E));
  not not_2 (not_2_out, IR[7]);
  CPU_DECODER_3_8 cpu_decoder_3_8_1 (
    .in_1(IR[6:4]), .out_9(cpu_decoder_3_8_1_out_9), .out_2(cpu_decoder_3_8_1_out_2),
    .out_3(cpu_decoder_3_8_1_out_3), .out_4(cpu_decoder_3_8_1_out_4), .out_5(cpu_decoder_3_8_1_out_5),
    .out_6(cpu_decoder_3_8_1_out_6), .out_7(cpu_decoder_3_8_1_out_7), .out_8(cpu_decoder_3_8_1_out_8));
  Decoder #(.select(4)) decoder_1 (
    .out0(HALT_t), .out1(decoder_1_out1), .out2(decoder_1_out2), .out3(decoder_1_out3),
    .out4(decoder_1_out4), .out5(decoder_1_out5), .out6(decoder_1_out6), .out7(decoder_1_out7),
    .out8(decoder_1_out8), .out9(decoder_1_out9), .out10(decoder_1_out10), .out11(decoder_1_out11),
    .out12(decoder_1_out12), .out13(decoder_1_out13), .out14(decoder_1_out14), .out15(decoder_1_out15),
    .sel({IR[6:4], IR[7]}), .en(ESC));
  CPU_DECODER_2_4 cpu_decoder_2_4_1 (
    .i(IR[1:0]), .out_2(cpu_decoder_2_4_1_out_2[0]), .out_3(cpu_decoder_2_4_1_out_2[1]),
    .out_4(cpu_decoder_2_4_1_out_2[2]), .out_5(cpu_decoder_2_4_1_out_2[3]));
  CPU_DECODER_2_4 cpu_decoder_2_4_2 (
    .i(IR[3:2]), .out_2(cpu_decoder_2_4_2_out_2[0]), .out_3(cpu_decoder_2_4_2_out_2[1]),
    .out_4(cpu_decoder_2_4_2_out_2[2]), .out_5(cpu_decoder_2_4_2_out_2[3]));
  not not_3 (not_3_out, LOAD_PROG);
  not not_4 (not_4_out, LOAD_PROG);
  CPU_DECODER_2_4 cpu_decoder_2_4_3 (
    .i(IR[1:0]), .out_2(cpu_decoder_2_4_3_out_2[0]), .out_3(cpu_decoder_2_4_3_out_2[1]),
    .out_4(cpu_decoder_2_4_3_out_2[2]), .out_5(cpu_decoder_2_4_3_out_2[3]));
  and and_19 (LOAD, not_2_out, not_5_out, cpu_decoder_3_8_1_out_2);
  and and_20 (STORE, not_2_out, not_5_out, cpu_decoder_3_8_1_out_3);
  and and_21 (DI, not_2_out, not_5_out, cpu_decoder_3_8_1_out_4);
  and and_22 (JMPR_RB, not_2_out, not_5_out, cpu_decoder_3_8_1_out_5);
  and and_23 (JMPR_A, not_2_out, not_5_out, cpu_decoder_3_8_1_out_6);
  and and_24 (JMPR_IF, not_2_out, not_5_out, cpu_decoder_3_8_1_out_7);
  and and_25 (CLF, not_2_out, not_5_out, cpu_decoder_3_8_1_out_8);
  and and_26 (and_26_out, not_2_out, not_5_out, cpu_decoder_3_8_1_out_9);
  not not_5 (not_5_out, ESC);
  and and_27 (and_27_out, clk, not_3_out);
  and and_28 (s1, not_4_out, cpu_stepper_1_s1);
  Pull_Resistor pull_resistor_7 (.node(REG_B_S));
  Pull_Resistor pull_resistor_8 (.node(s2));
  Pull_Resistor pull_resistor_9 (.node(s3));
  or or_5 (or_5_out, s1, s4);
  assign BUS1_S_t = or_5_out ? or_5_out : 1'bz;  // Controlled_Buffer controlled_buffer_1
  assign IAR_E_t = or_5_out ? or_5_out : 1'bz;  // Controlled_Buffer controlled_buffer_2
  assign MAR_S_t = or_5_out ? or_5_out : 1'bz;  // Controlled_Buffer controlled_buffer_3
  assign ACC_S_t = or_5_out ? or_5_out : 1'bz;  // Controlled_Buffer controlled_buffer_4
  and and_29 (R0_S, REG_B_S, cpu_decoder_2_4_3_out_2[0], clks);
  and and_30 (R1_S, REG_B_S, cpu_decoder_2_4_3_out_2[1], clks);
  and and_31 (R2_S, REG_B_S, cpu_decoder_2_4_3_out_2[2], clks);
  and and_32 (R3_S, REG_B_S, cpu_decoder_2_4_3_out_2[3], clks);
  CPU_FLAG_ESC cpu_flag_esc_1 (.i(and_26_out), .s(s3), .rst(s1), .o(ESC));
  Pull_Resistor pull_resistor_10 (.node(s4));
  Pull_Resistor pull_resistor_11 (.node(s5));
  assign RAM_E_t = or_6_out ? or_6_out : 1'bz;  // Controlled_Buffer controlled_buffer_5
  assign IR_S_t = or_6_out ? or_6_out : 1'bz;  // Controlled_Buffer controlled_buffer_6
  CPU_STEPPER cpu_stepper_1 (
    .rst(rst), .clk(and_27_out), .ESC(ESC), .s4(s4), .s5(s5), .s6(s6), .s7(s7), .s8(s8), .s9(s9),
    .s1(cpu_stepper_1_s1), .s2(s2), .s3(s3));
  Pull_Resistor pull_resistor_12 (.node(s6));
  Pull_Resistor pull_resistor_13 (.node(s7));
  or or_6 (or_6_out, s2, s5);
  Pull_Resistor pull_resistor_14 (.node(s9));
  Pull_Resistor pull_resistor_15 (.node(s8));
  assign IAR_S_t = or_7_out ? or_7_out : 1'bz;  // Controlled_Buffer controlled_buffer_7
  assign ACC_E_t = or_7_out ? or_7_out : 1'bz;  // Controlled_Buffer controlled_buffer_8
  not not_6 (not_6_out, ESC);
  assign REG_B_E = and_33_out ? and_33_out : 1'bz;  // Controlled_Buffer controlled_buffer_9
  assign TMP_S_t = and_33_out ? and_33_out : 1'bz;  // Controlled_Buffer controlled_buffer_10
  not not_7 (not_7_out, ESC);
  Pull_Resistor pull_resistor_16 (.node(ESC));
  or or_7 (or_7_out, s3, s6);
  and and_33 (and_33_out, s7, not_6_out, IR[7]);
  and and_34 (and_34_out, s7, not_7_out, DI);
  assign IAR_E_t = and_34_out ? and_34_out : 1'bz;  // Controlled_Buffer controlled_buffer_11
  assign MAR_S_t = and_34_out ? and_34_out : 1'bz;  // Controlled_Buffer controlled_buffer_12
  assign ACC_S_t = and_34_out ? and_34_out : 1'bz;  // Controlled_Buffer controlled_buffer_13
  assign BUS1_S_t = and_34_out ? and_34_out : 1'bz;  // Controlled_Buffer controlled_buffer_14
  and and_35 (and_35_out, s8, not_6_out, IR[7]);
  assign FLAG_S_t = and_35_out ? and_35_out : 1'bz;  // Controlled_Buffer controlled_buffer_15
  assign REG_A_E = and_35_out ? and_35_out : 1'bz;  // Controlled_Buffer controlled_buffer_16
  assign ACC_S_t = and_35_out ? and_35_out : 1'bz;  // Controlled_Buffer controlled_buffer_17
  assign RAM_E_t = and_37_out ? and_37_out : 1'bz;  // Controlled_Buffer controlled_buffer_18
  assign REG_B_S = and_37_out ? and_37_out : 1'bz;  // Controlled_Buffer controlled_buffer_19
  not not_8 (not_8_out, ESC);
  and and_36 (and_36_out, s7, not_8_out, CLF);
  assign FLAG_S_t = and_36_out ? and_36_out : 1'bz;  // Controlled_Buffer controlled_buffer_20
  assign BUS1_S_t = and_36_out ? and_36_out : 1'bz;  // Controlled_Buffer controlled_buffer_21
  assign ACC_E_t = and_38_out ? and_38_out : 1'bz;  // Controlled_Buffer controlled_buffer_22
  assign REG_B_S = and_38_out ? and_38_out : 1'bz;  // Controlled_Buffer controlled_buffer_23
  and and_37 (and_37_out, s8, not_7_out, DI);
  assign IAR_S_t = and_39_out ? and_39_out : 1'bz;  // Controlled_Buffer controlled_buffer_24
  assign ACC_E_t = and_39_out ? and_39_out : 1'bz;  // Controlled_Buffer controlled_buffer_25
  not not_9 (not_9_out, and_40_out);
  and and_38 (and_38_out, not_6_out, s9, IR[7], not_9_out);
  and and_39 (and_39_out, s9, not_7_out, DI);
  and and_40 (and_40_out, IR[4], IR[5], IR[6]);
  Pull_Resistor pull_resistor_17 (.node(IAR_S_t));
  Pull_Resistor pull_resistor_18 (.node(IR_S_t));
  Pull_Resistor pull_resistor_19 (.node(MAR_S_t));
  Pull_Resistor pull_resistor_20 (.node(ACC_S_t));
  Pull_Resistor pull_resistor_21 (.node(RAM_S_t));
  Pull_Resistor pull_resistor_22 (.node(TMP_S_t));
  Pull_Resistor pull_resistor_23 (.node(FLAG_S_t));
  not not_10 (not_10_out, ESC);
  assign MAR_S_t = and_48_out ? and_48_out : 1'bz;  // Controlled_Buffer controlled_buffer_26
  assign IAR_E_t = and_48_out ? and_48_out : 1'bz;  // Controlled_Buffer controlled_buffer_27
  assign ACC_S_t = and_48_out ? and_48_out : 1'bz;  // Controlled_Buffer controlled_buffer_28
  assign BUS1_S_t = and_48_out ? and_48_out : 1'bz;  // Controlled_Buffer controlled_buffer_29
  and and_41 (and_41_out, clks, IAR_S_t);
  and and_42 (and_42_out, clks, IR_S_t);
  and and_43 (and_43_out, clks, MAR_S_t);
  and and_44 (and_44_out, clks, ACC_S_t);
  and and_45 (and_45_out, clks, RAM_S_t);
  and and_46 (and_46_out, clks, TMP_S_t);
  and and_47 (and_47_out, clks, FLAG_S_t);
  assign controlled_buffer_30_out = STORE ? STORE : 1'bz;  // Controlled_Buffer controlled_buffer_30
  not not_11 (not_11_out, ESC);
  Pull_Resistor pull_resistor_24 (.node(controlled_buffer_30_out));
  and and_48 (and_48_out, s7, not_10_out, JMPR_IF);
  assign controlled_buffer_30_out = LOAD ? LOAD : 1'bz;  // Controlled_Buffer controlled_buffer_31
  and and_49 (and_49_out, controlled_buffer_30_out, not_11_out, s7);
  assign REG_A_E = and_49_out ? and_49_out : 1'bz;  // Controlled_Buffer controlled_buffer_32
  assign MAR_S_t = and_49_out ? and_49_out : 1'bz;  // Controlled_Buffer controlled_buffer_33
  and and_50 (and_50_out, s8, not_10_out, JMPR_IF);
  assign ACC_E_t = and_50_out ? and_50_out : 1'bz;  // Controlled_Buffer controlled_buffer_34
  or or_8 (IAR_S, rst, and_41_out);
  or or_9 (IR_S, rst, and_42_out);
  and and_51 (and_51_out, clke, LOAD_PROG);
  or or_10 (MAR_S, and_51_out, and_43_out);
  or or_11 (ACC_S, rst, and_44_out);
  and and_52 (and_52_out, clks, LOAD_PROG);
  or or_12 (RAM_S, and_52_out, and_45_out);
  or or_13 (TMP_S, rst, and_46_out);
  or or_14 (FLAG_S, rst, and_47_out);
  and and_53 (and_53_out, STORE, not_11_out, s8);
  not not_12 (not_12_out, ESC);
  and and_54 (and_54_out, s7, not_12_out, JMPR_RB);
  assign REG_B_E = and_54_out ? and_54_out : 1'bz;  // Controlled_Buffer controlled_buffer_35
  assign IAR_S_t = and_54_out ? and_54_out : 1'bz;  // Controlled_Buffer controlled_buffer_36
  and and_55 (and_55_out, JMPR_IF, s9, not_10_out, or_16_out);
  assign RAM_E_t = and_55_out ? and_55_out : 1'bz;  // Controlled_Buffer controlled_buffer_37
  or or_15 (or_15_out, and_50_out, and_55_out);
  assign IAR_S_t = or_15_out ? or_15_out : 1'bz;  // Controlled_Buffer controlled_buffer_38
  assign RAM_S_t = and_53_out ? and_53_out : 1'bz;  // Controlled_Buffer controlled_buffer_39
  assign REG_B_E = and_53_out ? and_53_out : 1'bz;  // Controlled_Buffer controlled_buffer_40
  or or_16 (or_16_out, and_57_out, and_58_out, and_59_out, and_60_out);
  and and_56 (and_56_out, LOAD, not_11_out, s8);
  assign RAM_E_t = and_56_out ? and_56_out : 1'bz;  // Controlled_Buffer controlled_buffer_41
  assign REG_B_S = and_56_out ? and_56_out : 1'bz;  // Controlled_Buffer controlled_buffer_42
  and and_57 (and_57_out, FLAG_C, IR[3]);
  and and_58 (and_58_out, FLAG_A, IR[2]);
  and and_59 (and_59_out, FLAG_E, IR[1]);
  and and_60 (and_60_out, FLAG_Z, IR[0]);
  Pull_Resistor pull_resistor_25 (.node(HALT_t));
  not not_13 (not_13_out, ESC);
  assign MAR_S_t = and_62_out ? and_62_out : 1'bz;  // Controlled_Buffer controlled_buffer_43
  assign IAR_E_t = and_62_out ? and_62_out : 1'bz;  // Controlled_Buffer controlled_buffer_44
  and and_61 (HALT, HALT_t, ESC, s7);
  and and_62 (and_62_out, s7, not_13_out, JMPR_A);
  and and_63 (and_63_out, s8, not_13_out, JMPR_A);
  assign RAM_E_t = and_63_out ? and_63_out : 1'bz;  // Controlled_Buffer controlled_buffer_45
  assign IAR_S_t = and_63_out ? and_63_out : 1'bz;  // Controlled_Buffer controlled_buffer_46

  // Other names for the same wires on the sheet: IR_0 = IR[0]; IR_1 = IR[1]; IR_2 = IR[2]; IR_3 = IR[3]; IR_4 = IR[4];
  //   IR_5 = IR[5]; IR_6 = IR[6]; ALU_FLAG = IR[7]; IR_7 = IR[7]

  // Notes on the sheet:
  //   OPCODES
  //   FETCH
  //   STAGE 1 - 3: FETCH CYCLE
  //   STAGE 4 - 7: EXECUTE
  //   EXECUTE
  //   FETCH
  //   ALU EXECUTION
  //   DATA INSTRUCTION
  //   CLEAR FLAGS
  //   LOAD/STORE
  //   JUMP REGISTER
  //   JUMPIF INSTRUCTION
  //   HALT
  //   JUMP ADDRESS
endmodule

module CPU_STEPPER (
  input  rst,
  input  ESC,
  input  clk,
  output s1,
  output s2,
  output s3,
  output s4,
  output s5,
  output s6,
  output s7,
  output s8,
  output s9
);

  wire controlled_buffer_1_out, demultiplexer_1_out0, demultiplexer_1_out1;

  D_Flip_Flop #(.trigger("falling")) d_ff_1 (.D(s9), .clk(clk), .Q(s1), .preset(rst));  // open: Qn, reset
  D_Flip_Flop #(.trigger("falling")) d_ff_2 (.D(s1), .clk(clk), .Q(s2), .reset(rst));  // open: Qn, preset
  Pull_Resistor pull_resistor_1 (.node(s1));
  Pull_Resistor pull_resistor_2 (.node(s2));
  D_Flip_Flop #(.trigger("falling")) d_ff_3 (.D(s2), .clk(clk), .Q(s3), .reset(rst));  // open: Qn, preset
  Demultiplexer demultiplexer_1 (.out0(demultiplexer_1_out0), .out1(demultiplexer_1_out1), .in(s3), .sel(ESC));
  Pull_Resistor pull_resistor_3 (.node(s3));
  D_Flip_Flop #(.trigger("falling")) d_ff_4 (
    .D(demultiplexer_1_out1), .clk(clk), .Q(s4), .reset(rst));  // open: Qn, preset
  D_Flip_Flop #(.trigger("falling")) d_ff_5 (.D(s4), .clk(clk), .Q(s5), .reset(rst));  // open: Qn, preset
  Pull_Resistor pull_resistor_4 (.node(s4));
  assign controlled_buffer_1_out = demultiplexer_1_out0 ? demultiplexer_1_out0 : 1'bz;  // Controlled_Buffer controlled_buffer_1
  Pull_Resistor pull_resistor_5 (.node(s5));
  D_Flip_Flop #(.trigger("falling")) d_ff_6 (.D(s5), .clk(clk), .Q(s6), .reset(rst));  // open: Qn, preset
  assign controlled_buffer_1_out = s6 ? s6 : 1'bz;  // Controlled_Buffer controlled_buffer_2
  D_Flip_Flop #(.trigger("falling")) d_ff_7 (
    .D(controlled_buffer_1_out), .clk(clk), .Q(s7), .reset(rst));  // open: Qn, preset
  Pull_Resistor pull_resistor_6 (.node(controlled_buffer_1_out));
  D_Flip_Flop #(.trigger("falling")) d_ff_8 (.D(s7), .clk(clk), .Q(s8), .reset(rst));  // open: Qn, preset
  Pull_Resistor pull_resistor_7 (.node(s7));
  D_Flip_Flop #(.trigger("falling")) d_ff_9 (.D(s8), .clk(clk), .Q(s9), .reset(rst));  // open: Qn, preset
  Pull_Resistor pull_resistor_8 (.node(s8));
  Pull_Resistor pull_resistor_9 (.node(s9));
endmodule

module CPU_IAR (
  input  [7:0] i,
  input  e,
  input  s,
  output [7:0] r,
  output [7:0] o
);

  wire [7:0] cpu_enable_1_o;

  CPU_MEM_8 cpu_mem_8_1 (.i(i), .s(s), .o(r));  // open: rst
  assign o = e ? cpu_enable_1_o : 8'bz;  // Controlled_Buffer controlled_buffer_1
  CPU_ENABLE cpu_enable_1 (.i(r), .e(e), .o(cpu_enable_1_o));
endmodule

module CPU_IR (
  input  [7:0] i,
  input  s,
  output [7:0] o
);

  CPU_MEM_8 cpu_mem_8_1 (.i(i), .s(s), .o(o));  // open: rst
endmodule

module CPU (
  input  [7:0] BUS_DATA_INSERT,
  input  BUS_DATA_INSERT_E,
  input  R0_S,
  input  R1_S,
  input  R2_S,
  input  R3_S,
  input  CLK,
  input  rst,
  input  LOAD_PROG,
  input  rst_RAM,
  input  IR_S,
  input  [7:0] PROG_D,
  output [7:0] BUS_DATA,
  output [7:0] R0,
  output [7:0] R1,
  output [7:0] R2,
  output [7:0] R3,
  output s1,
  output s2,
  output s3,
  output s4,
  output s5,
  output s6,
  output s7,
  output s8,
  output s9,
  output [7:0] IR,
  output [7:0] ACC,
  output [7:0] PC
);

  wire ALU_a_greater, ALU_c_out, ALU_equal, ALU_zero, and_1_out, CLK_t, controlled_buffer_3_out,
       controlled_buffer_5_out, controlled_buffer_7_out, controlled_buffer_9_out, controlled_buffer_11_out,
       cpu_clk_1_clke, cpu_clk_1_clks, cpu_control_section_1_acc_e, cpu_control_section_1_acc_s,
       cpu_control_section_1_alu_0, cpu_control_section_1_alu_1, cpu_control_section_1_alu_2,
       cpu_control_section_1_bus1_s, cpu_control_section_1_flag_s, cpu_control_section_1_iar_e,
       cpu_control_section_1_iar_s, cpu_control_section_1_ir_s, cpu_control_section_1_mar_s,
       cpu_control_section_1_r0_e, cpu_control_section_1_r0_s, cpu_control_section_1_r1_e,
       cpu_control_section_1_r1_s, cpu_control_section_1_r2_e, cpu_control_section_1_r2_s,
       cpu_control_section_1_r3_e, cpu_control_section_1_r3_s, cpu_control_section_1_ram_e,
       cpu_control_section_1_ram_s, cpu_control_section_1_tmp_s, FLAGS_out_6, FLAGS_out_7, FLAGS_out_8,
       FLAGS_out_9, HALT, not_1_out, not_2_out;
  wire [7:0] ALU_o, BUS1_o, cpu_cnt_256_1_out_7, multiplexer_1_out, TMP_o;

  CPU_TMP TMP (.i(BUS_DATA), .s(cpu_control_section_1_tmp_s), .o(TMP_o));
  CPU_BUS1 BUS1 (.i(TMP_o), .bus1(cpu_control_section_1_bus1_s), .o(BUS1_o));
  CPU_ALU ALU (
    .c_in(1'b0), .a(BUS_DATA), .b(BUS1_o), .ALU_0(cpu_control_section_1_alu_0),
    .ALU_1(cpu_control_section_1_alu_1), .ALU_2(cpu_control_section_1_alu_2), .equal(ALU_equal),
    .a_greater(ALU_a_greater), .c_out(ALU_c_out), .o(ALU_o), .zero(ALU_zero));
  CPU_ACCUMULATOR cpu_accumulator_1 (
    .i(ALU_o), .s(cpu_control_section_1_acc_s), .e(cpu_control_section_1_acc_e), .r(ACC), .o(BUS_DATA));
  CPU_FLAG FLAGS (
    .C(ALU_c_out), .A(ALU_a_greater), .E(ALU_equal), .Z(ALU_zero), .FLAG_S(cpu_control_section_1_flag_s),
    .out_6(FLAGS_out_6), .out_7(FLAGS_out_7), .out_8(FLAGS_out_8), .out_9(FLAGS_out_9));
  not not_1 (not_1_out, HALT);
  not not_2 (not_2_out, LOAD_PROG);
  assign BUS_DATA = BUS_DATA_INSERT_E ? BUS_DATA_INSERT : 8'bz;  // Controlled_Buffer controlled_buffer_1
  CPU_CLK cpu_clk_1 (.clkin(and_1_out), .clk(CLK_t), .clks(cpu_clk_1_clks), .clke(cpu_clk_1_clke));
  and and_1 (and_1_out, CLK, not_1_out);
  CPU_CNT_256 cpu_cnt_256_1 (
    .RST(not_2_out), .C(LOAD_PROG), .E(LOAD_PROG), .CLK(CLK_t), .out_7(cpu_cnt_256_1_out_7));  // open: LOAD, in_6
  assign BUS_DATA = LOAD_PROG ? cpu_cnt_256_1_out_7 : 8'bz;  // Controlled_Buffer controlled_buffer_2
  CPU_CONTROL_SECTION cpu_control_section_1 (
    .rst(rst), .FLAG_C(FLAGS_out_6), .FLAG_A(FLAGS_out_7), .FLAG_E(FLAGS_out_8), .FLAG_Z(FLAGS_out_9),
    .clks(cpu_clk_1_clks), .clk(CLK_t), .clke(cpu_clk_1_clke), .IR(IR), .LOAD_PROG(LOAD_PROG), .s9(s9),
    .R0_E(cpu_control_section_1_r0_e), .R1_E(cpu_control_section_1_r1_e), .R2_E(cpu_control_section_1_r2_e),
    .R3_E(cpu_control_section_1_r3_e), .IAR_S(cpu_control_section_1_iar_s),
    .IR_S(cpu_control_section_1_ir_s), .MAR_S(cpu_control_section_1_mar_s),
    .ACC_S(cpu_control_section_1_acc_s), .RAM_S(cpu_control_section_1_ram_s),
    .TMP_S(cpu_control_section_1_tmp_s), .FLAG_S(cpu_control_section_1_flag_s), .HALT(HALT),
    .BUS1_S(cpu_control_section_1_bus1_s), .RAM_E(cpu_control_section_1_ram_e),
    .ACC_E(cpu_control_section_1_acc_e), .IAR_E(cpu_control_section_1_iar_e),
    .ALU_0(cpu_control_section_1_alu_0), .ALU_1(cpu_control_section_1_alu_1),
    .ALU_2(cpu_control_section_1_alu_2), .s1(s1), .s2(s2), .s3(s3), .s4(s4),
    .R0_S(cpu_control_section_1_r0_s), .R1_S(cpu_control_section_1_r1_s), .R2_S(cpu_control_section_1_r2_s),
    .R3_S(cpu_control_section_1_r3_s), .s5(s5), .s6(s6), .s7(s7), .s8(s8));
  assign controlled_buffer_3_out = R0_S ? R0_S : 1'bz;  // Controlled_Buffer controlled_buffer_3
  assign controlled_buffer_3_out = cpu_control_section_1_r0_s ? cpu_control_section_1_r0_s : 1'bz;  // Controlled_Buffer controlled_buffer_4
  CPU_REG_8 cpu_reg_8_1 (
    .i(BUS_DATA), .s(controlled_buffer_3_out), .e(cpu_control_section_1_r0_e), .o(BUS_DATA), .r(R0));  // open: rst
  assign controlled_buffer_5_out = R1_S ? R1_S : 1'bz;  // Controlled_Buffer controlled_buffer_5
  assign controlled_buffer_5_out = cpu_control_section_1_r1_s ? cpu_control_section_1_r1_s : 1'bz;  // Controlled_Buffer controlled_buffer_6
  CPU_IAR cpu_iar_1 (
    .i(BUS_DATA), .s(cpu_control_section_1_iar_s), .e(cpu_control_section_1_iar_e), .r(PC), .o(BUS_DATA));
  CPU_REG_8 cpu_reg_8_2 (
    .i(BUS_DATA), .s(controlled_buffer_5_out), .e(cpu_control_section_1_r1_e), .o(BUS_DATA), .r(R1));  // open: rst
  assign controlled_buffer_7_out = R2_S ? R2_S : 1'bz;  // Controlled_Buffer controlled_buffer_7
  assign controlled_buffer_7_out = cpu_control_section_1_r2_s ? cpu_control_section_1_r2_s : 1'bz;  // Controlled_Buffer controlled_buffer_8
  assign controlled_buffer_9_out = cpu_control_section_1_ir_s ? cpu_control_section_1_ir_s : 1'bz;  // Controlled_Buffer controlled_buffer_9
  CPU_IR cpu_ir_1 (.i(BUS_DATA), .s(controlled_buffer_9_out), .o(IR));
  assign controlled_buffer_9_out = IR_S ? IR_S : 1'bz;  // Controlled_Buffer controlled_buffer_10
  CPU_REG_8 cpu_reg_8_3 (
    .i(BUS_DATA), .s(controlled_buffer_7_out), .e(cpu_control_section_1_r2_e), .o(BUS_DATA), .r(R2));  // open: rst
  assign controlled_buffer_11_out = R3_S ? R3_S : 1'bz;  // Controlled_Buffer controlled_buffer_11
  assign controlled_buffer_11_out = cpu_control_section_1_r3_s ? cpu_control_section_1_r3_s : 1'bz;  // Controlled_Buffer controlled_buffer_12
  CPU_REG_8 cpu_reg_8_4 (
    .i(BUS_DATA), .s(controlled_buffer_11_out), .e(cpu_control_section_1_r3_e), .o(BUS_DATA), .r(R3));  // open: rst
  Multiplexer #(.width(8)) multiplexer_1 (.in0(BUS_DATA), .in1(PROG_D), .out(multiplexer_1_out), .sel(LOAD_PROG));
  RAM_256 RAM (
    .address(BUS_DATA), .sa(cpu_control_section_1_mar_s), .s(cpu_control_section_1_ram_s),
    .e(cpu_control_section_1_ram_e), .rst(rst_RAM), .i(multiplexer_1_out), .o(BUS_DATA));  // open: out_26, out_10, out_27, out_11, out_28, out_12, out_29, out_13, out_30, out_14, out_31, out_15, out_32, out_16, out_33, out_17, out_34, out_18, out_35, out_19, out_36, out_20, out_37, out_21, out_38, out_22, out_39, out_23, out_24, out_8, out_25, out_9
  Pull_Resistor pull_resistor_1 (.node(BUS_DATA[7]));
  Pull_Resistor pull_resistor_2 (.node(BUS_DATA[6]));
  Pull_Resistor pull_resistor_3 (.node(BUS_DATA[5]));
  Pull_Resistor pull_resistor_4 (.node(BUS_DATA[4]));
  Pull_Resistor pull_resistor_5 (.node(BUS_DATA[3]));
  Pull_Resistor pull_resistor_6 (.node(BUS_DATA[2]));
  Pull_Resistor pull_resistor_7 (.node(BUS_DATA[1]));
  Pull_Resistor pull_resistor_8 (.node(BUS_DATA[0]));
endmodule

module CPU_FLAG (
  input  C,
  input  A,
  input  E,
  input  Z,
  input  FLAG_S,
  output out_6,
  output out_7,
  output out_8,
  output out_9
);

  D_Flip_Flop #(.trigger("high")) d_ff_1 (.D(C), .clk(FLAG_S), .Q(out_6));  // open: Qn, preset, reset
  D_Flip_Flop #(.trigger("high")) d_ff_2 (.D(A), .clk(FLAG_S), .Q(out_7));  // open: Qn, preset, reset
  D_Flip_Flop #(.trigger("high")) d_ff_3 (.D(E), .clk(FLAG_S), .Q(out_8));  // open: Qn, preset, reset
  D_Flip_Flop #(.trigger("high")) d_ff_4 (.D(Z), .clk(FLAG_S), .Q(out_9));  // open: Qn, preset, reset
endmodule

module CPU_CNT_256 (
  input  RST,
  input  LOAD,
  input  C,
  input  E,
  input  CLK,
  input  [7:0] in_6,
  output [7:0] out_7
);

  Counter #(.trigger("falling")) counter_1 (
    .clr(RST), .load(LOAD), .up(C), .count(E), .clk(CLK), .D(in_6), .Q(out_7));  // open: carry
endmodule

module CPU_FLAG_ESC (
  input  i,
  input  s,
  input  rst,
  output o
);

  D_Flip_Flop d_ff_1 (.D(i), .clk(s), .Q(o), .reset(rst));  // open: Qn, preset
endmodule
